// Logisim project ALU32.circ as structural Verilog
module ALU32 (
  input  [31:0] A,
  input  [31:0] B,
  input  [3:0] Op,
  input  [4:0] Sa,
  output [31:0] C,
  output V
);

  wire [31:0] addsubop_1_c, compareop_1_c, logicalop_1_c, shiftop_1_c;

  LogicalOp logicalop_1 (.A(A), .B(B), .Op(Op), .C(logicalop_1_c));
  CompareOp compareop_1 (.B(B), .A(A), .Op(Op), .C(compareop_1_c));
  AddSubOp addsubop_1 (.A(A), .Op(Op), .B(B), .V(V), .C(addsubop_1_c));
  ShiftOp shiftop_1 (.B(B), .Op(Op), .Sa(Sa), .C(shiftop_1_c));
  assign C = logicalop_1_c | compareop_1_c | addsubop_1_c | shiftop_1_c;  // OR_Gate or_1, 32 bits wide
endmodule

module Add32 (
  input  [31:0] A,
  input  [31:0] B,
  input  Cin,
  output V,
  output [31:0] C
);

  wire add16_1_cout;

  Add16 add16_1 (.A(A[15:0]), .B(B[15:0]), .Cin(Cin), .Cout(add16_1_cout), .Sout(C[15:0]));
  Add16V add16v_1 (.A(A[31:16]), .B(B[31:16]), .Cin(add16_1_cout), .V(V), .Sout(C[31:16]));
endmodule

module LeftShift32 (
  input  [31:0] B,
  input  Cin,
  input  [4:0] Sa,
  output [31:0] C
);

  wire [0:0] bit_extender_5_out;
  wire [1:0] bit_extender_4_out;
  wire [3:0] bit_extender_3_out;
  wire [7:0] bit_extender_2_out;
  wire [15:0] bit_extender_1_out;
  wire [31:0] multiplexer_1_out, multiplexer_2_out, multiplexer_4_out;
  wire [31:2] multiplexer_3_out_2;
  wire [31:30] multiplexer_3_out;

  assign bit_extender_1_out = {{15{Cin}}, Cin};  // Bit_Extender bit_extender_1
  Multiplexer #(.width(32), .enable("false")) multiplexer_1 (
    .in0(B), .in1({B[15:0], bit_extender_1_out}), .out(multiplexer_1_out), .sel(Sa[4]));
  Bit_Extender #(.in_width(16), .out_width(8)) bit_extender_2 (.in(bit_extender_1_out), .out(bit_extender_2_out));
  Multiplexer #(.width(32), .enable("false")) multiplexer_2 (
    .in0(multiplexer_1_out), .in1({multiplexer_1_out[23:0], bit_extender_2_out}), .out(multiplexer_2_out),
    .sel(Sa[3]));
  Bit_Extender #(.out_width(4)) bit_extender_3 (.in(bit_extender_2_out), .out(bit_extender_3_out));
  Multiplexer #(.width(32), .enable("false")) multiplexer_3 (
    .in0(multiplexer_2_out), .in1({multiplexer_2_out[27:0], bit_extender_3_out}),
    .out({multiplexer_3_out, multiplexer_3_out_2}), .sel(Sa[2]));
  Bit_Extender #(.in_width(4), .out_width(2)) bit_extender_4 (.in(bit_extender_3_out), .out(bit_extender_4_out));
  Multiplexer #(.width(32), .enable("false")) multiplexer_4 (
    .in0({multiplexer_3_out, multiplexer_3_out_2}), .in1({multiplexer_3_out_2, bit_extender_4_out}),
    .out(multiplexer_4_out), .sel(Sa[1]));
  Bit_Extender #(.in_width(2), .out_width(1)) bit_extender_5 (.in(bit_extender_4_out), .out(bit_extender_5_out[0]));
  Multiplexer #(.width(32), .enable("false")) multiplexer_5 (
    .in0(multiplexer_4_out), .in1({multiplexer_4_out[30:0], bit_extender_5_out[0]}), .out(C), .sel(Sa[0]));
endmodule

module LogicalOp (
  input  [31:0] A,
  input  [31:0] B,
  input  [3:0] Op,
  output [31:0] C
);

  wire and_2_out, and_3_out, or_2_out;
  wire [31:0] and_1_out, not_1_out, or_1_out, xor_1_out;

  assign and_1_out = A & B;  // AND_Gate and_1, 32 bits wide
  assign or_1_out = A | B;  // OR_Gate or_1, 32 bits wide
  assign xor_1_out = A ^ B;  // XOR_Gate xor_1, 32 bits wide
  assign not_1_out = ~or_1_out;  // NOT_Gate not_1, 32 bits wide
  and and_2 (and_2_out, Op[1], ~Op[2], Op[3]);  // AND_Gate
  and and_3 (and_3_out, ~Op[1], Op[2], ~Op[3]);  // AND_Gate
  or or_2 (or_2_out, and_2_out, and_3_out);
  Multiplexer #(.select(2), .width(32)) multiplexer_1 (
    .in0(and_1_out), .in1(or_1_out), .in2(xor_1_out), .in3(not_1_out), .out(C), .sel(Op[1:0]), .en(or_2_out));
endmodule

module CompareOp (
  input  [31:0] B,
  input  [31:0] A,
  input  [3:0] Op,
  output [31:0] C
);

  wire and_4_out, and_5_out, and_7_out, and_8_out, and_9_out, not_2_out, not_3_out, or_1_out;
  wire [1:0] and_3_out, and_6_out;
  wire [7:0] and_1_out, and_2_out;
  wire [31:0] bit_extender_1_out, bit_extender_2_out, bit_extender_3_out, bit_extender_4_out, not_1_out,
       xnor_1_out;

  assign not_1_out = ~A;  // NOT_Gate not_1, 32 bits wide
  assign xnor_1_out = ~(B ^ A);  // XNOR_Gate xnor_1, 32 bits wide
  assign and_1_out = not_1_out[7:0] & not_1_out[15:8] & not_1_out[23:16] & not_1_out[31:24];  // AND_Gate and_1, 8 bits wide
  assign and_2_out = xnor_1_out[7:0] & xnor_1_out[15:8] & xnor_1_out[23:16] & xnor_1_out[31:24];  // AND_Gate and_2, 8 bits wide
  assign and_3_out = and_1_out[1:0] & and_1_out[3:2] & and_1_out[5:4] & and_1_out[7:6];  // AND_Gate and_3, 2 bits wide
  and and_4 (and_4_out, ~Op[1], ~Op[2], Op[3]);  // AND_Gate
  and and_5 (and_5_out, Op[1], Op[2], Op[3]);
  assign and_6_out = and_2_out[1:0] & and_2_out[3:2] & and_2_out[5:4] & and_2_out[7:6];  // AND_Gate and_6, 2 bits wide
  and and_7 (and_7_out, and_3_out[0], and_3_out[1]);
  or or_1 (or_1_out, and_4_out, and_5_out);
  and and_8 (and_8_out, and_6_out[0], and_6_out[1]);
  and and_9 (and_9_out, ~A[31], ~and_7_out);  // AND_Gate
  not not_2 (not_2_out, and_8_out);
  assign bit_extender_1_out = {{31{1'b0}}, not_2_out};  // Bit_Extender bit_extender_1
  assign bit_extender_2_out = {{31{1'b0}}, and_8_out};  // Bit_Extender bit_extender_2
  not not_3 (not_3_out, and_9_out);
  assign bit_extender_3_out = {{31{1'b0}}, not_3_out};  // Bit_Extender bit_extender_3
  assign bit_extender_4_out = {{31{1'b0}}, and_9_out};  // Bit_Extender bit_extender_4
  Multiplexer #(.select(2), .width(32)) multiplexer_1 (
    .in0(bit_extender_1_out), .in1(bit_extender_2_out), .in2(bit_extender_3_out), .in3(bit_extender_4_out),
    .out(C), .sel(Op[1:0]), .en(or_1_out));

  // Notes on the sheet:
  //   If A==B, A XNOR B = 1
  //   If A>0, A 31th bit will be 0
  //   If A>0, at least 1 bit (0-30th) will be 1
  //   C = 0 if the OpCode is not Compare Op
endmodule

module AddSubOp (
  input  [31:0] A,
  input  [3:0] Op,
  input  [31:0] B,
  output V,
  output [31:0] C
);

  wire and_1_out, and_2_out;
  wire [31:0] and_3_out, and_4_out, bit_extender_1_out, bit_extender_2_out, xor_1_out;

  assign bit_extender_1_out = {{31{and_1_out}}, and_1_out};  // Bit_Extender bit_extender_1
  and and_1 (and_1_out, Op[1], ~Op[3]);  // AND_Gate
  assign bit_extender_2_out = {{31{Op[2]}}, Op[2]};  // Bit_Extender bit_extender_2
  assign xor_1_out = bit_extender_2_out ^ B;  // XOR_Gate xor_1, 32 bits wide
  and and_2 (and_2_out, and_1_out, Op[2]);
  assign and_3_out = A & bit_extender_1_out;  // AND_Gate and_3, 32 bits wide
  assign and_4_out = bit_extender_1_out & xor_1_out;  // AND_Gate and_4, 32 bits wide
  Add32 add32_1 (.A(and_3_out), .B(and_4_out), .Cin(and_2_out), .V(V), .C(C));
endmodule

module ShiftOp (
  input  [31:0] B,
  input  [3:0] Op,
  input  [4:0] Sa,
  output [31:0] C
);

  wire and_1_out, and_2_out, and_3_out, and_4_out, mirror_1_signbit, or_1_out;
  wire [4:0] and_5_out, bit_extender_1_out;
  wire [31:0] leftshift32_1_c, mirror_1_b_mirror, mirror_2_b_mirror, multiplexer_1_out;

  Mirror mirror_1 (.B(B), .B_Mirror(mirror_1_b_mirror), .SignBit(mirror_1_signbit));
  and and_1 (and_1_out, mirror_1_signbit, Op[0]);
  and and_2 (and_2_out, ~Op[1], ~Op[2], ~Op[3]);  // AND_Gate
  and and_3 (and_3_out, ~Op[1], Op[2], Op[3]);  // AND_Gate
  Multiplexer #(.width(32)) multiplexer_1 (
    .in0(B), .in1(mirror_1_b_mirror), .out(multiplexer_1_out), .sel(Op[2]), .en(or_1_out));
  or or_1 (or_1_out, and_2_out, and_3_out);
  and and_4 (and_4_out, and_1_out, Op[2]);
  assign bit_extender_1_out = {{4{or_1_out}}, or_1_out};  // Bit_Extender bit_extender_1
  assign and_5_out = bit_extender_1_out & Sa;  // AND_Gate and_5, 5 bits wide
  LeftShift32 leftshift32_1 (.B(multiplexer_1_out), .Cin(and_4_out), .Sa(and_5_out), .C(leftshift32_1_c));
  Mirror mirror_2 (.B(leftshift32_1_c), .B_Mirror(mirror_2_b_mirror));  // open: SignBit
  Multiplexer #(.width(32), .enable("false")) multiplexer_2 (
    .in0(leftshift32_1_c), .in1(mirror_2_b_mirror), .out(C), .sel(Op[2]));
endmodule

module Mirror (
  input  [31:0] B,
  output [31:0] B_Mirror,
  output SignBit
);


  assign B_Mirror = {B[0], B[1], B[2], B[3], B[4], B[5], B[6], B[7], B[8], B[9], B[10], B[11], B[12], B[13], B[14], B[15], B[16], B[17], B[18], B[19], B[20], B[21], B[22], B[23], B[24], B[25], B[26], B[27], B[28], B[29], B[30], B[31]};
  assign SignBit = B[31];
endmodule

module Add1 (
  input  A,
  input  B,
  input  Cin,
  output Sout,
  output Cout
);

  wire and_1_out, and_2_out, xor_1_out;

  xor xor_1 (xor_1_out, A, B);
  and and_1 (and_1_out, A, B);
  xor xor_2 (Sout, xor_1_out, Cin);
  and and_2 (and_2_out, xor_1_out, Cin);
  or or_1 (Cout, and_2_out, and_1_out);
endmodule

module Add2 (
  input  [1:0] A,
  input  [1:0] B,
  input  Cin,
  output Cout,
  output [1:0] Sout
);

  wire add1_1_cout;

  Add1 add1_1 (.A(A[0]), .B(B[0]), .Cin(Cin), .Sout(Sout[0]), .Cout(add1_1_cout));
  Add1 add1_2 (.A(A[1]), .B(B[1]), .Cin(add1_1_cout), .Sout(Sout[1]), .Cout(Cout));
endmodule

module Add2V (
  input  [1:0] A,
  input  [1:0] B,
  input  Cin,
  output V,
  output [1:0] Sout
);

  wire add1_1_cout, add1_2_cout;

  Add1 add1_1 (.A(A[0]), .B(B[0]), .Cin(Cin), .Sout(Sout[0]), .Cout(add1_1_cout));
  Add1 add1_2 (.A(A[1]), .B(B[1]), .Cin(add1_1_cout), .Sout(Sout[1]), .Cout(add1_2_cout));
  xor xor_1 (V, add1_2_cout, add1_1_cout);
endmodule

module Add4 (
  input  [3:0] A,
  input  [3:0] B,
  input  Cin,
  output Cout,
  output [3:0] Sout
);

  wire add2_1_cout;

  Add2 add2_1 (.A(A[1:0]), .B(B[1:0]), .Cin(Cin), .Cout(add2_1_cout), .Sout(Sout[1:0]));
  Add2 add2_2 (.A(A[3:2]), .B(B[3:2]), .Cin(add2_1_cout), .Cout(Cout), .Sout(Sout[3:2]));
endmodule

module Add4V (
  input  [3:0] A,
  input  [3:0] B,
  input  Cin,
  output V,
  output [3:0] Sout
);

  wire add2_1_cout;

  Add2 add2_1 (.A(A[1:0]), .B(B[1:0]), .Cin(Cin), .Cout(add2_1_cout), .Sout(Sout[1:0]));
  Add2V add2v_1 (.A(A[3:2]), .B(B[3:2]), .Cin(add2_1_cout), .V(V), .Sout(Sout[3:2]));
endmodule

module Add8 (
  input  [7:0] A,
  input  [7:0] B,
  input  Cin,
  output Cout,
  output [7:0] Sout
);

  wire add4_1_cout;

  Add4 add4_1 (.A(A[3:0]), .B(B[3:0]), .Cin(Cin), .Cout(add4_1_cout), .Sout(Sout[3:0]));
  Add4 add4_2 (.A(A[7:4]), .B(B[7:4]), .Cin(add4_1_cout), .Cout(Cout), .Sout(Sout[7:4]));
endmodule

module Add8V (
  input  [7:0] A,
  input  [7:0] B,
  input  Cin,
  output V,
  output [7:0] Sout
);

  wire add4_1_cout;

  Add4 add4_1 (.A(A[3:0]), .B(B[3:0]), .Cin(Cin), .Cout(add4_1_cout), .Sout(Sout[3:0]));
  Add4V add4v_1 (.A(A[7:4]), .B(B[7:4]), .Cin(add4_1_cout), .V(V), .Sout(Sout[7:4]));
endmodule

module Add16 (
  input  [15:0] A,
  input  [15:0] B,
  input  Cin,
  output Cout,
  output [15:0] Sout
);

  wire add8_1_cout;

  Add8 add8_1 (.A(A[7:0]), .B(B[7:0]), .Cin(Cin), .Cout(add8_1_cout), .Sout(Sout[7:0]));
  Add8 add8_2 (.A(A[15:8]), .B(B[15:8]), .Cin(add8_1_cout), .Cout(Cout), .Sout(Sout[15:8]));
endmodule

module Add16V (
  input  [15:0] A,
  input  [15:0] B,
  input  Cin,
  output V,
  output [15:0] Sout
);

  wire add8_1_cout;

  Add8 add8_1 (.A(A[7:0]), .B(B[7:0]), .Cin(Cin), .Cout(add8_1_cout), .Sout(Sout[7:0]));
  Add8V add8v_1 (.A(A[15:8]), .B(B[15:8]), .Cin(add8_1_cout), .V(V), .Sout(Sout[15:8]));
endmodule
