// Logisim project Add32.circ as structural Verilog
module Add32 (
  input  [31:0] A,
  input  [31:0] B,
  input  Cin,
  output V,
  output [31:0] C
);

  wire add16_1_cout;

  Add16 add16_1 (.A(A[15:0]), .B(B[15:0]), .Cin(Cin), .Cout(add16_1_cout), .Sout(C[15:0]));
  Add16V add16v_1 (.A(A[31:16]), .B(B[31:16]), .Cin(add16_1_cout), .V(V), .Sout(C[31:16]));
endmodule

module Add1 (
  input  A,
  input  B,
  input  Cin,
  output Sout,
  output Cout
);

  wire and_1_out, and_2_out, xor_1_out;

  xor xor_1 (xor_1_out, A, B);
  and and_1 (and_1_out, A, B);
  xor xor_2 (Sout, xor_1_out, Cin);
  and and_2 (and_2_out, xor_1_out, Cin);
  or or_1 (Cout, and_2_out, and_1_out);
endmodule

module Add2 (
  input  [1:0] A,
  input  [1:0] B,
  input  Cin,
  output Cout,
  output [1:0] Sout
);

  wire add1_1_cout;

  Add1 add1_1 (.A(A[0]), .B(B[0]), .Cin(Cin), .Sout(Sout[0]), .Cout(add1_1_cout));
  Add1 add1_2 (.A(A[1]), .B(B[1]), .Cin(add1_1_cout), .Sout(Sout[1]), .Cout(Cout));
endmodule

module Add2V (
  input  [1:0] A,
  input  [1:0] B,
  input  Cin,
  output V,
  output [1:0] Sout
);

  wire add1_1_cout, add1_2_cout;

  Add1 add1_1 (.A(A[0]), .B(B[0]), .Cin(Cin), .Sout(Sout[0]), .Cout(add1_1_cout));
  Add1 add1_2 (.A(A[1]), .B(B[1]), .Cin(add1_1_cout), .Sout(Sout[1]), .Cout(add1_2_cout));
  xor xor_1 (V, add1_2_cout, add1_1_cout);
endmodule

module Add4 (
  input  [3:0] A,
  input  [3:0] B,
  input  Cin,
  output Cout,
  output [3:0] Sout
);

  wire add2_1_cout;

  Add2 add2_1 (.A(A[1:0]), .B(B[1:0]), .Cin(Cin), .Cout(add2_1_cout), .Sout(Sout[1:0]));
  Add2 add2_2 (.A(A[3:2]), .B(B[3:2]), .Cin(add2_1_cout), .Cout(Cout), .Sout(Sout[3:2]));
endmodule

module Add4V (
  input  [3:0] A,
  input  [3:0] B,
  input  Cin,
  output V,
  output [3:0] Sout
);

  wire add2_1_cout;

  Add2 add2_1 (.A(A[1:0]), .B(B[1:0]), .Cin(Cin), .Cout(add2_1_cout), .Sout(Sout[1:0]));
  Add2V add2v_1 (.A(A[3:2]), .B(B[3:2]), .Cin(add2_1_cout), .V(V), .Sout(Sout[3:2]));
endmodule

module Add8 (
  input  [7:0] A,
  input  [7:0] B,
  input  Cin,
  output Cout,
  output [7:0] Sout
);

  wire add4_1_cout;

  Add4 add4_1 (.A(A[3:0]), .B(B[3:0]), .Cin(Cin), .Cout(add4_1_cout), .Sout(Sout[3:0]));
  Add4 add4_2 (.A(A[7:4]), .B(B[7:4]), .Cin(add4_1_cout), .Cout(Cout), .Sout(Sout[7:4]));
endmodule

module Add8V (
  input  [7:0] A,
  input  [7:0] B,
  input  Cin,
  output V,
  output [7:0] Sout
);

  wire add4_1_cout;

  Add4 add4_1 (.A(A[3:0]), .B(B[3:0]), .Cin(Cin), .Cout(add4_1_cout), .Sout(Sout[3:0]));
  Add4V add4v_1 (.A(A[7:4]), .B(B[7:4]), .Cin(add4_1_cout), .V(V), .Sout(Sout[7:4]));
endmodule

module Add16 (
  input  [15:0] A,
  input  [15:0] B,
  input  Cin,
  output Cout,
  output [15:0] Sout
);

  wire add8_1_cout;

  Add8 add8_1 (.A(A[7:0]), .B(B[7:0]), .Cin(Cin), .Cout(add8_1_cout), .Sout(Sout[7:0]));
  Add8 add8_2 (.A(A[15:8]), .B(B[15:8]), .Cin(add8_1_cout), .Cout(Cout), .Sout(Sout[15:8]));
endmodule

module Add16V (
  input  [15:0] A,
  input  [15:0] B,
  input  Cin,
  output V,
  output [15:0] Sout
);

  wire add8_1_cout;

  Add8 add8_1 (.A(A[7:0]), .B(B[7:0]), .Cin(Cin), .Cout(add8_1_cout), .Sout(Sout[7:0]));
  Add8V add8v_1 (.A(A[15:8]), .B(B[15:8]), .Cin(add8_1_cout), .V(V), .Sout(Sout[15:8]));
endmodule
