// Logisim project LeftShift32.circ as structural Verilog: 1 circuit, main circuit main
module main (
  input  [31:0] B,
  input  [4:0] Sa,
  input  Cin
);

  wire [15:0] bit_extender_1_out;
  wire [31:0] multiplexer_1_out;

  assign bit_extender_1_out = {{15{Cin}}, Cin};  // Bit_Extender bit_extender_1
  Multiplexer #(.width(32), .enable("false")) multiplexer_1 (
    .in0(B), .in1({B[15:0], bit_extender_1_out}), .out(multiplexer_1_out), .sel(Sa[4]));
endmodule
